# Fritzing sketch Uno and Ky-002 (saved by Fritzing 0.9.3b)

parts:
  Part1 = Arduino Uno (Rev3)
  Part4 = KY-002 Vibration Switch Module [package="Breakout board"]

nets:
  N1: Part1.D11_PWM/MOSI, Part4.S
  N2: Part1.GND, Part4.-
  5V: Part1.5V, Part4.Vin

custom parts:
  KY-002 Vibration Switch Module: Arduino Vibration Switch Module KY-002 Keyes allows detection of shock and vibration.
