# Fritzing sketch Uno and Ky-009 (saved by Fritzing 0.9.3b)

parts:
  Part1 = Arduino Uno (Rev3)
  Part3 = KY-009 Full Color RGB LED SMD Module [package="Breakout board"]

nets:
  N1: Part1.D9_PWM, Part3.G
  N2: Part1.D10_PWM/SS, Part3.B
  N3: Part1.D11_PWM/MOSI, Part3.R
  N4: Part1.GND, Part3.-

custom parts:
  KY-009 Full Color RGB LED SMD Module: RGB full color LED Module KY-009 for Arduino, emits a range of colors by mixing red, green and blue. The amount of each primary color is adjusted using PWM.
