# Fritzing sketch Uno and Ky-013 (saved by Fritzing 0.9.3b)

parts:
  Part1 = Arduino Uno (Rev3)
  Mod1 = KY-013 Analog Temperature Sensor Module [package="Breakout board"]

nets:
  N1: Part1.A0, Mod1.S
  5V: Part1.5V, Mod1.Vin
  N2: Part1.GND, Mod1.-

custom parts:
  KY-013 Analog Temperature Sensor Module: KY-013 Analog Temperature Sensor module, measures ambient temperature based on resistance of the thermistor.
