# Fritzing sketch Uno and Ky-018 (saved by Fritzing 0.9.3b)

parts:
  Part1 = Arduino Uno (Rev3)
  Part2 = KY-018 Photoresistor Module [package="Breakout board"]

nets:
  N1: Part1.A1, Part2.S
  5V: Part1.5V, Part2.Vin
  N2: Part1.GND, Part2.-

custom parts:
  KY-018 Photoresistor Module: KY-018 Photoresistor module, used to measure light intensity. It can determine the presence or absence of light.
