# Fritzing sketch Uno and Ky-020 (saved by Fritzing 0.9.3b)

parts:
  Part1 = Arduino Uno (Rev3)
  Part4 = KY-020 Tilt Switch Module [package="Breakout board"]

nets:
  N1: Part1.D2, Part4.S
  5V: Part1.5V, Part4.Vin
  N2: Part1.GND, Part4.-

custom parts:
  KY-020 Tilt Switch Module: KY-020 Arduino tilt switch sensor module. Closes the circuit when it is tilted to the side as long as it is moved with enough force and degree of inclination to activate the ball switch inside.
