# Fritzing sketch Uno and Ky-023 (saved by Fritzing 0.9.3b)

parts:
  Part1 = Arduino Uno (Rev3)
  Part2 = KY-023 Dual Axis Joystick Module [package="Breakout board"]

nets:
  N1: Part1.A1, Part2.VRx
  N2: Part1.A2, Part2.VRy
  N3: Part1.D2, Part2.SW
  5V: Part1.5V, Part2.+5V
  GND: Part1.GND, Part2.GND
