# Fritzing sketch Uno and Ky-029 (saved by Fritzing 0.9.3b)

parts:
  Part1 = Arduino Uno (Rev3)
  Mod1 = KY-029 Dual Color LED Module [package="Breakout board"]
  R1 = Resistor [tolerance=±5% resistance=220 package=THT]
  R2 = Resistor [tolerance=±5% resistance=220 package=THT]

nets:
  N1: Part1.D10_PWM/SS, R2.Pin_0
  N2: Part1.D11_PWM/MOSI, R1.Pin_0
  N3: Part1.GND, Mod1.G
  N4: Mod1.R, R1.Pin_1
  N5: Mod1.-, R2.Pin_1

custom parts:
  KY-029 Dual Color LED Module: KY-029 Dual Color LED Module consist of a common cathode 5mm red/green LED.
