# Fritzing sketch Uno and Ky-031 (saved by Fritzing 0.9.3b)

parts:
  Part1 = Arduino Uno (Rev3)
  Mod1 = KY-031 Knock Sensor Module [package="Breakout board"]

nets:
  N1: Part1.D2, Mod1.S
  5V: Part1.5V, Mod1.Vin
  N2: Part1.GND, Mod1.-

custom parts:
  KY-031 Knock Sensor Module: KY-031 Knock Sensor module. A vibration sensor that sends a signal when a knock/tap is detected.
