# Fritzing sketch Uno and Ky-034 (saved by Fritzing 0.9.3b)

parts:
  Part1 = Arduino Uno (Rev3)
  Mod2 = KY-034 Automatic Flashing Color LED [package="Breakout board"]

nets:
  N1: Part1.D11_PWM/MOSI, Mod2.S
  N2: Part1.GND, Mod2.-

custom parts:
  KY-034 Automatic Flashing Color LED: KY-034 Automatic Flashiing Color LED. A 7 color LED that flashes through a sequence of colors, creating a multicolored pattern of flashing light.
